# Fritzing sketch adc_tb (saved by Fritzing 0.9.6b)
breadboards: 1

parts:
  R2 = Rotary Potentiometer (Small) [maximum_resistance=100kΩ package=THT]
  R3 = Resistor [tolerance=±5% power=0.25 resistance=100 package=THT]
  SEG0 = 7 Segment Display
  JP1 = Header 10 [package=1x10-2mm-smd]
  JP2 = Header 10 [package=1x10-2mm-smd]
  JC1 = Header 10 [package=1x10-2mm-smd]
  JP4 = Header 10 [package=1x10-2mm-smd]
  LED1 = smd LED [color="Red (633nm)" package="0603 [SMD]"]
  SEG2 = 7 Segment Display
  VCC = Battery block 9V
  S3 = Momentary Switch [package=ksa_sealed_tac_switch]
  R4 = Resistor [tolerance=±5% power=0.25 resistance=100 package=THT]
  SEG1 = 7 Segment Display

nets:
  N1: R2.leg1, SEG0.common_anode, SEG0.Segment_DP, JP1.5, JP1.8, JP2.1, JP2.4, JP2.7, JC1.5, JC1.8, JP4.1, JP4.4, JP4.7, LED1.cathode, SEG2.common_anode, SEG2.Segment_DP, VCC.-, R4.Pin_1, SEG1.common_anode, SEG1.Segment_DP
  N2: R2.wiper, JP2.9, LED1.anode
  N3: R2.leg2, JP1.2, VCC.+, S3.1
  N4: R3.Pin_0, JP4.9
  N5: R3.Pin_1, JP2.8
  N6: SEG0.Segment_E, JP1.6
  N7: SEG0.Segment_D, JP1.4
  N8: SEG0.Segment_C, JP1.3
  N9: SEG0.Segment_B, JC1.2
  N10: SEG0.Segment_A, JC1.3
  N11: SEG0.Segment_F, JC1.4
  N12: SEG0.Segment_G, JC1.6
  N13: JP1.7, SEG1.Segment_C
  N14: JP1.9, SEG1.Segment_D
  N15: JP1.10, SEG1.Segment_E
  N16: JP2.2, SEG2.Segment_C
  N17: JP2.3, SEG2.Segment_D
  N18: JP2.5, SEG2.Segment_E
  N19: JP2.6, S3.4, R4.Pin_0
  N20: JC1.7, SEG1.Segment_B
  N21: JC1.9, SEG1.Segment_A
  N22: JC1.10, SEG1.Segment_F
  N23: JP4.2, SEG1.Segment_G
  N24: JP4.3, SEG2.Segment_B
  N25: JP4.5, SEG2.Segment_A
  N26: JP4.6, SEG2.Segment_F
  N27: JP4.8, SEG2.Segment_G

notes:
  1
  39
  40
  2
  2.5V
